// Logisim project Atv_Sistemas.circ as structural Verilog: 1 circuit, main circuit main
module main (
  input  A,
  input  B,
  input  C,
  input  D,
  output G,
  output E,
  output F,
  output H,
  output I,
  output J,
  output K,
  output N,
  output L,
  output M,
  output O,
  output P,
  output Q,
  output R,
  output S,
  output T,
  output U,
  output V,
  output W,
  output X,
  output Y
);

  wire and_1_out, and_2_out, and_3_out, and_4_out, and_5_out, and_6_out, and_7_out, and_8_out, and_9_out,
       and_10_out, and_11_out, and_12_out, and_13_out, and_14_out, and_15_out, and_16_out, and_17_out,
       and_18_out, and_19_out, and_20_out, and_21_out, and_22_out, and_23_out, and_24_out, and_25_out,
       and_26_out, and_27_out, and_28_out, and_29_out, and_30_out, and_31_out, and_32_out, and_33_out,
       and_34_out, and_35_out, and_36_out, and_37_out, and_38_out, and_39_out, and_40_out, and_41_out,
       and_42_out, and_43_out, and_44_out, and_45_out, nand_1_out, nor_3_out, nor_4_out, not_1_out,
       not_4_out, or_7_out, or_8_out, or_9_out, or_10_out, or_11_out, or_12_out, or_13_out, or_14_out,
       or_15_out, or_16_out, or_17_out, or_18_out, or_19_out, or_20_out, or_21_out, or_22_out, or_23_out,
       or_24_out, or_25_out, or_26_out, or_27_out, or_28_out, or_29_out, or_30_out, or_31_out, or_32_out,
       or_33_out, or_34_out, xor_1_out, xor_2_out;

  not not_1 (not_1_out, A);
  not not_2 (P, B);
  not not_3 (I, D);
  not not_4 (not_4_out, C);
  or or_1 (E, I, C);
  nor nor_1 (H, D, C);
  or or_2 (J, I, D);
  or or_3 (K, not_4_out, D);
  or or_4 (L, P, A);
  nor nor_2 (O, A, B);
  or or_5 (Q, P, B);
  or or_6 (R, not_1_out, B);
  or or_7 (or_7_out, C, I);
  xor xor_1 (xor_1_out, D, C);
  or or_8 (or_8_out, not_4_out, D);
  or or_9 (or_9_out, D, C);
  or or_10 (or_10_out, D, I);
  or or_11 (or_11_out, C, I);
  xor xor_2 (xor_2_out, D, C);
  or or_12 (or_12_out, D, not_4_out);
  or or_13 (or_13_out, C, I);
  nor nor_3 (nor_3_out, D, C);
  and and_1 (and_1_out, C, D);
  or or_14 (or_14_out, C, D);
  and and_2 (and_2_out, not_4_out, D);
  nor nor_4 (nor_4_out, C, D);
  and and_3 (and_3_out, D, C);
  or or_15 (or_15_out, D, I);
  or or_16 (or_16_out, D, I);
  nand nand_1 (nand_1_out, D, C);
  or or_17 (or_17_out, D, not_4_out);
  or or_18 (or_18_out, I, C);
  or or_19 (or_19_out, C, D);
  or or_20 (or_20_out, D, I);
  and and_4 (and_4_out, P, or_7_out);
  and and_5 (and_5_out, or_7_out, B);
  and and_6 (and_6_out, B, xor_1_out);
  and and_7 (and_7_out, P, or_8_out);
  and and_8 (and_8_out, C, P);
  and and_9 (and_9_out, or_9_out, B);
  and and_10 (and_10_out, or_10_out, P);
  and and_11 (and_11_out, or_10_out, B);
  and and_12 (and_12_out, or_11_out, P);
  and and_13 (and_13_out, xor_2_out, B);
  and and_14 (and_14_out, or_12_out, P);
  and and_15 (and_15_out, or_13_out, B);
  and and_16 (and_16_out, nor_3_out, P);
  and and_17 (and_17_out, and_1_out, B);
  and and_18 (and_18_out, C, P);
  and and_19 (and_19_out, or_14_out, B);
  and and_20 (and_20_out, I, P);
  and and_21 (and_21_out, and_2_out, B);
  and and_22 (and_22_out, nor_4_out, P);
  and and_23 (and_23_out, and_3_out, B);
  and and_24 (and_24_out, or_15_out, P);
  and and_25 (and_25_out, or_16_out, B);
  and and_26 (and_26_out, nand_1_out, P);
  and and_27 (and_27_out, not_4_out, B);
  and and_28 (and_28_out, or_17_out, P);
  and and_29 (and_29_out, or_18_out, B);
  and and_30 (and_30_out, or_19_out, or_19_out, P);
  and and_31 (and_31_out, or_20_out, B);
  or or_21 (or_21_out, and_4_out, and_6_out);
  or or_22 (or_22_out, and_5_out, and_7_out);
  or or_23 (or_23_out, and_8_out, and_9_out);
  or or_24 (or_24_out, and_10_out, and_11_out);
  or or_25 (or_25_out, and_12_out, and_13_out);
  or or_26 (or_26_out, and_14_out, and_15_out);
  or or_27 (or_27_out, and_16_out, and_17_out);
  or or_28 (or_28_out, and_18_out, and_19_out);
  or or_29 (or_29_out, and_20_out, and_21_out);
  or or_30 (or_30_out, and_22_out, and_23_out);
  or or_31 (or_31_out, and_24_out, and_25_out);
  or or_32 (or_32_out, and_26_out, and_27_out);
  or or_33 (or_33_out, and_28_out, and_29_out);
  or or_34 (or_34_out, and_30_out, and_31_out);
  _7_Segment_Display u_7_segment_display_1 (.g(C), .f(H), .a(E), .b(J), .e(I), .d(E), .c(K));  // open: dp
  _7_Segment_Display u_7_segment_display_2 (.g(A), .f(O), .a(L), .b(Q), .e(P), .d(L), .c(R));  // open: dp
  and and_32 (and_32_out, or_21_out, not_1_out);
  and and_33 (and_33_out, A, or_22_out);
  and and_34 (and_34_out, or_23_out, not_1_out);
  and and_35 (and_35_out, A, or_24_out);
  and and_36 (and_36_out, or_25_out, not_1_out);
  and and_37 (and_37_out, A, or_26_out);
  and and_38 (and_38_out, or_27_out, not_1_out);
  and and_39 (and_39_out, A, or_28_out);
  and and_40 (and_40_out, or_29_out, not_1_out);
  and and_41 (and_41_out, A, or_30_out);
  and and_42 (and_42_out, or_31_out, not_1_out);
  and and_43 (and_43_out, A, or_32_out);
  and and_44 (and_44_out, or_33_out, not_1_out);
  and and_45 (and_45_out, A, or_34_out);
  or or_35 (S, and_32_out, and_33_out);
  or or_36 (T, and_34_out, and_35_out);
  or or_37 (U, and_36_out, and_37_out);
  or or_38 (V, and_38_out, and_39_out);
  or or_39 (W, and_40_out, and_41_out);
  or or_40 (X, and_42_out, and_43_out);
  or or_41 (Y, and_44_out, and_45_out);
  _7_Segment_Display u_7_segment_display_3 (.g(T), .f(V), .a(S), .b(X), .e(W), .d(U), .c(Y));  // open: dp

  assign F = C;
  assign G = E;
  assign M = A;
  assign N = L;
endmodule
